// Logisim project Project.circ as structural Verilog: 1 circuit, main circuit main
module main (
  input  in_1,
  output [3:0] out_2
);

  wire and_1_out, and_2_out, and_3_out, and_4_out, and_5_out, and_6_out, clock_1_out, decoder_1_out0,
       decoder_1_out1, decoder_1_out2, decoder_1_out3, decoder_1_out4, decoder_1_out5, decoder_1_out6,
       decoder_1_out7, decoder_1_out8, decoder_1_out9, decoder_1_out10, decoder_1_out11, decoder_1_out12,
       decoder_1_out13, Dot_out, f_out, j_k_ff_1_qn, j_k_ff_2_qn, j_k_ff_3_qn, not_1_out, or_1_out, or_2_out,
       or_3_out, or_4_out, or_5_out, or_6_out, or_7_out, or_8_out, or_9_out, or_10_out, or_11_out, or_12_out,
       or_13_out, or_14_out, or_15_out, or_16_out, or_17_out, or_18_out, or_19_out, or_20_out, or_21_out,
       or_22_out, or_23_out, or_24_out, or_25_out, or_26_out, or_27_out, or_28_out;

  Clock clock_1 (.out(clock_1_out));
  Decoder #(.select(4), .enable("false")) decoder_1 (
    .out0(decoder_1_out0), .out1(decoder_1_out1), .out2(decoder_1_out2), .out3(decoder_1_out3),
    .out4(decoder_1_out4), .out5(decoder_1_out5), .out6(decoder_1_out6), .out7(decoder_1_out7),
    .out8(decoder_1_out8), .out9(decoder_1_out9), .out10(decoder_1_out10), .out11(decoder_1_out11),
    .out12(decoder_1_out12), .out13(decoder_1_out13), .sel(out_2));  // open: out14, out15
  not not_1 (not_1_out, in_1);
  J_K_Flip_Flop j_k_ff_1 (
    .J(1'b1), .clk(clock_1_out), .K(1'b1), .Q(out_2[0]), .Qn(j_k_ff_1_qn), .en(1'b1));  // open: preset, reset
  and and_1 (and_1_out, not_1_out, out_2[0]);
  and and_2 (and_2_out, j_k_ff_1_qn, in_1);
  or or_1 (or_1_out, and_1_out, and_2_out);
  J_K_Flip_Flop j_k_ff_2 (
    .J(or_1_out), .clk(clock_1_out), .K(or_1_out), .Q(out_2[1]), .Qn(j_k_ff_2_qn), .en(1'b1));  // open: preset, reset
  and and_3 (and_3_out, and_1_out, out_2[1]);
  and and_4 (and_4_out, j_k_ff_2_qn, and_2_out);
  or or_2 (or_2_out, and_3_out, and_4_out);
  or or_3 (or_3_out, decoder_1_out1, decoder_1_out2, decoder_1_out5);
  or or_4 (or_4_out, decoder_1_out6, decoder_1_out7, decoder_1_out8);
  or or_5 (or_5_out, decoder_1_out10, decoder_1_out11, decoder_1_out12);
  or or_6 (or_6_out, decoder_1_out13, decoder_1_out12, decoder_1_out10);
  or or_7 (or_7_out, decoder_1_out8, decoder_1_out7, decoder_1_out5);
  or or_8 (or_8_out, decoder_1_out3, decoder_1_out1, decoder_1_out0);
  or or_9 (or_9_out, decoder_1_out13, decoder_1_out11, decoder_1_out8);
  or or_10 (or_10_out, decoder_1_out7, decoder_1_out6, decoder_1_out3);
  or or_11 (or_11_out, decoder_1_out2, decoder_1_out1, decoder_1_out0);
  or or_12 (or_12_out, decoder_1_out12, decoder_1_out11, decoder_1_out10);
  or or_13 (or_13_out, decoder_1_out8, decoder_1_out6, decoder_1_out5);
  or or_14 (or_14_out, decoder_1_out2, decoder_1_out1);
  or or_15 (or_15_out, decoder_1_out12, decoder_1_out11, decoder_1_out10);
  or or_16 (or_16_out, decoder_1_out5, decoder_1_out2, decoder_1_out1);
  or or_17 (or_17_out, decoder_1_out13, decoder_1_out11, decoder_1_out6);
  or or_18 (or_18_out, decoder_1_out3, decoder_1_out2, decoder_1_out1);
  or or_19 (or_19_out, decoder_1_out13, decoder_1_out12, decoder_1_out11);
  or or_20 (or_20_out, decoder_1_out10, decoder_1_out8, decoder_1_out6);
  or or_21 (or_21_out, decoder_1_out5, decoder_1_out3, decoder_1_out2);
  or or_22 (or_22_out, or_3_out, or_4_out, or_5_out);
  or or_23 (or_23_out, or_6_out, or_7_out, or_8_out);
  or or_24 (or_24_out, or_9_out, or_10_out, or_11_out);
  or or_25 (or_25_out, or_12_out, or_13_out, or_14_out);
  or or_26 (or_26_out, or_15_out, or_16_out);
  or f (f_out, or_17_out, or_18_out);
  or or_27 (or_27_out, or_19_out, or_20_out, or_21_out);
  or Dot (Dot_out, decoder_1_out9, decoder_1_out4);
  J_K_Flip_Flop j_k_ff_3 (
    .J(or_2_out), .clk(clock_1_out), .K(or_2_out), .Q(out_2[2]), .Qn(j_k_ff_3_qn), .en(1'b1));  // open: preset, reset
  and and_5 (and_5_out, and_3_out, out_2[2]);
  and and_6 (and_6_out, j_k_ff_3_qn, and_4_out);
  or or_28 (or_28_out, and_5_out, and_6_out);
  J_K_Flip_Flop j_k_ff_4 (
    .J(or_28_out), .clk(clock_1_out), .K(or_28_out), .Q(out_2[3]), .en(1'b1));  // open: Qn, preset, reset
  _7_Segment_Display u_7_segment_display_1 (
    .g(or_27_out), .f(f_out), .a(or_22_out), .b(or_23_out), .e(or_26_out), .d(or_25_out), .c(or_24_out),
    .dp(Dot_out));

  // Notes on the sheet:
  //   1064.2573.2624
endmodule
